# Fritzing sketch raPID_FC_mini (saved by Fritzing 0.9.3b)
circuit board: 5.18188cm x 2.83576cm
breadboards: 1

parts:
  Teensy_3_2 = Teensy 3.1
  MPU-6050 = MPU-6050 Board GY-521 [form="♀ (female)" package=THT]
  VIN = female pin header, 2 pins [form="♀ (female)"]
  RX = female pin header, 2 pins [form="♀ (female)"]
  J3 = female pin header, 4 pins [form="♀ (female)"]
  J4 = female pin header, 4 pins [form="♀ (female)"]
  J5 = female pin header, 6 pins [form="♀ (female)"]

nets:
  N1: Teensy_3_2.GND, MPU-6050.pin2, VIN.pin1, RX.pin2
  N2: Teensy_3_2.D3, J3.pin4
  N3: Teensy_3_2.D4, J3.pin3
  N4: Teensy_3_2.D5, J3.pin2
  N5: Teensy_3_2.D6, J3.pin1
  N6: Teensy_3_2.D7, J5.pin6
  N7: Teensy_3_2.D8, J5.pin5
  N8: Teensy_3_2.D9, J5.pin4
  N9: Teensy_3_2.D10, J5.pin3
  N10: Teensy_3_2.D11, J5.pin2
  N11: Teensy_3_2.D12, J5.pin1
  N12: Teensy_3_2.A0/D14, MPU-6050.pin8
  N13: Teensy_3_2.A4/D18, MPU-6050.pin4
  N14: Teensy_3_2.A5/D19, MPU-6050.pin3
  N15: Teensy_3_2.3V3, MPU-6050.pin1, J4.pin1, J4.pin2, J4.pin3, J4.pin4
  N16: Teensy_3_2.Vin, VIN.pin2, RX.pin1

custom parts:
  MPU-6050 Board GY-521: Acelerometro y Giroscopio MPU-6050 Board GY-521
